# Fritzing sketch 3LED (saved by Fritzing 0.9.3b)
breadboards: 1

parts:
  Raspberry_Pi_1 = Raspberry Pi 3 [part_number=RPI-3-V1.2]
  LED1 = LED - 3mm [color="Red (633nm)" package="3 mm [THT]"]
  R1 = Resistor [tolerance=±5% resistance=220 package="1206 [SMD]"]
  LED2 = LED - 3mm [color="Orange (612nm)" package="3 mm [THT]"]
  LED3 = LED - 3mm [color="Green (570nm)" package="3 mm [THT]"]

nets:
  N1: Raspberry_Pi_1.GIPO25, LED2.anode
  N2: Raspberry_Pi_1.GIPO24, LED3.anode
  N3: Raspberry_Pi_1.GIPO23, LED1.anode
  N4: Raspberry_Pi_1.GND, R1.Pin_1
  N5: LED1.cathode, R1.Pin_0, LED2.cathode, LED3.cathode
