# Fritzing sketch Btn+LED (saved by Fritzing 0.9.3b)
breadboards: 1

parts:
  Raspberry_Pi_1 = Raspberry Pi 3 [part_number=RPI-3-V1.2]
  LED1 = LED - 3mm [color="Red (633nm)" package="3 mm [THT]"]
  R1 = Resistor [tolerance=±5% resistance=220 package="1206 [SMD]"]
  S1 = Pushbutton [package="[THT]"]

nets:
  N1: Raspberry_Pi_1.GIPO21, Raspberry_Pi_1.GND, R1.Pin_1, S1.Pin_3, S1.Pin_4
  N2: Raspberry_Pi_1.GIPO14, LED1.anode
  N3: Raspberry_Pi_1.5V, S1.Pin_1, S1.Pin_2
  N4: LED1.cathode, R1.Pin_0
