# Fritzing sketch Jeu_Buttons (saved by Fritzing 0.9.3b)
breadboards: 1

parts:
  LED1 = LED - 5mm [color="Red (633nm)" package="5 mm [THT]"]
  S1 = Momentary Switch [package=ksa_sealed_tac_switch]
  S2 = Momentary Switch [package=ksa_sealed_tac_switch]
  R1 = Resistor [tolerance=±5% resistance=220 package="0603 [SMD]"]
  Raspberry_Pi_1 = Raspberry Pi 3 [part_number=RPI-3-V1.2]

nets:
  N1: LED1.cathode, R1.Pin_0
  N2: LED1.anode, Raspberry_Pi_1.GPIO21
  N3: S1.2, S2.2, Raspberry_Pi_1.5V
  N4: S1.3, Raspberry_Pi_1.GPIO14
  N5: S1.4, S2.4, R1.Pin_1, Raspberry_Pi_1.GND
  N6: S2.3, Raspberry_Pi_1.GPIO15
