# Fritzing sketch LED (saved by Fritzing 0.9.3b)
breadboards: 1

parts:
  Raspberry_Pi_1 = Raspberry Pi 3 [part_number=RPI-3-V1.2]
  LED1 = LED - 3mm [color="Red (633nm)" package="3 mm [THT]"]
  R1 = Resistor [tolerance=±5% resistance=220 package="1206 [SMD]"]

nets:
  N1: Raspberry_Pi_1.GIPO25, LED1.anode
  N2: Raspberry_Pi_1.GND, R1.Pin_1
  N3: LED1.cathode, R1.Pin_0
